# Fritzing sketch Line (saved by Fritzing 0.9.2b)
breadboards: 1

parts:
  IC1 = L293D [package=THT]
  M1 = DC Motor
  Part1 = Arduino Uno (Rev3)
  M2 = DC Motor
  J1 = Infrared Proximity Sensor
  J2 = Infrared Proximity Sensor
  J3 = Infrared Proximity Sensor

nets:
  VCC: IC1.Enable_1, IC1.Enable_2, IC1.+V, Part1.5V, J1.Vcc, J2.Vcc, J3.Vcc
  N1: IC1.In_1, Part1.D3_PWM
  N2: IC1.Out_1_(_Controlled_by_Enable_1_), M1.pin_2
  GND: IC1.0V, Part1.GND, J1.GND, J2.GND, J3.GND
  N3: IC1.Out_2_(_Controlled_by_Enable_1_), M1.pin_1
  N4: IC1.In_2, Part1.D5_PWM
  N5: IC1.+Vmotor, Part1.VIN
  N6: IC1.In_3, Part1.D6_PWM
  N7: IC1.Out_3_(_Controlled_by_Enable_2_), M2.pin_2
  N8: IC1.Out_4_(_Controlled_by_Enable_2_), M2.pin_1
  N9: IC1.In_4, Part1.D9_PWM
  N10: Part1.D10_PWM/SS, J3.Vout
  N11: Part1.D11_PWM/MOSI, J1.Vout
  N12: Part1.D12/MISO, J2.Vout
